// Logisim project comparator.circ as structural Verilog: 1 circuit, main circuit main
module main (
  input  A,
  input  B,
  output A___B,
  output A___B_2,
  output A___B_3
);

  wire not_1_out, not_2_out;

  not not_1 (not_1_out, A);
  not not_2 (not_2_out, B);
  and and_1 (A___B, A, not_2_out);
  and and_2 (A___B_2, not_1_out, B);
  xnor xnor_1 (A___B_3, A, B);
endmodule
