// Logisim project mux.circ as structural Verilog: 1 circuit, main circuit main
module main (
  input  I0,
  input  I1,
  input  I2,
  input  I3,
  input  S0,
  input  S1,
  output Y
);

  wire and_1_out, and_2_out, and_3_out, and_4_out, not_1_out, not_2_out, or_1_out, or_2_out;

  not not_1 (not_1_out, S1);
  not not_2 (not_2_out, S0);
  and and_1 (and_1_out, I0, not_2_out, not_1_out);
  and and_2 (and_2_out, I1, not_1_out, S0);
  and and_3 (and_3_out, I2, S1, not_2_out);
  and and_4 (and_4_out, I3, S0, S1);
  or or_1 (or_1_out, and_1_out, and_2_out);
  or or_2 (or_2_out, and_3_out, and_4_out);
  or or_3 (Y, or_1_out, or_2_out);
endmodule
